// Digital circuit adder.dig as structural Verilog
module adder (
  input  ClockIn,
  input  CarryFlag,
  input  [7:0] LHS,
  input  [7:0] RHS,
  input  CarrySelectA,
  input  CarrySelectB,
  input  ALU__Assert,
  output CarryOut,
  output [7:0] AdderOut,
  output [7:0] MainBusOut
);

  wire Adder_Low_pin9, CarrySelected;

  _74253 Carry_Selection (
    .pin1(1'b0), .pin2(CarrySelectB), .pin3(1'b0), .pin4(1'b1), .pin5(CarryFlag), .pin6(1'b0),
    .pin7(CarrySelected), .pin8(1'b0), .pin9(1'b0), .pin10(1'b0), .pin11(1'b0), .pin12(1'b0), .pin13(1'b0),
    .pin14(CarrySelectA), .pin15(1'b0), .pin16(1'b1));
  _74283 Adder_Low (
    .pin1(AdderOut[1]), .pin2(RHS[1]), .pin3(LHS[1]), .pin4(AdderOut[0]), .pin5(LHS[0]), .pin6(RHS[0]),
    .pin7(CarrySelected), .pin8(1'b0), .pin9(Adder_Low_pin9), .pin10(AdderOut[3]), .pin11(RHS[3]),
    .pin12(LHS[3]), .pin13(AdderOut[2]), .pin14(LHS[2]), .pin15(RHS[2]), .pin16(1'b1));
  _74283 Adder_High (
    .pin1(AdderOut[5]), .pin2(RHS[5]), .pin3(LHS[5]), .pin4(AdderOut[4]), .pin5(LHS[4]), .pin6(RHS[4]),
    .pin7(Adder_Low_pin9), .pin8(1'b0), .pin9(CarryOut), .pin10(AdderOut[7]), .pin11(RHS[7]), .pin12(LHS[7]),
    .pin13(AdderOut[6]), .pin14(LHS[6]), .pin15(RHS[6]), .pin16(1'b1));
  _74541 Main_Bus_Driver (
    .pin1(ALU__Assert), .pin2(AdderOut[7]), .pin3(AdderOut[6]), .pin4(AdderOut[5]), .pin5(AdderOut[4]),
    .pin6(AdderOut[3]), .pin7(AdderOut[2]), .pin8(AdderOut[1]), .pin9(AdderOut[0]), .pin10(1'b0),
    .pin11(MainBusOut[0]), .pin12(MainBusOut[1]), .pin13(MainBusOut[2]), .pin14(MainBusOut[3]),
    .pin15(MainBusOut[4]), .pin16(MainBusOut[5]), .pin17(MainBusOut[6]), .pin18(MainBusOut[7]), .pin19(1'b0),
    .pin20(1'b1));

  // Notes on the sheet:
  //   Carry Selection
endmodule

/* Test case Basic Tests:
ClockIn LHS RHS CarryFlag CarrySelectB CarrySelectA CarryOut AdderOut

# clear to predictable state
0       0   0   0         0            1            x        x
1       0   0   0         0            1            0        0

# add two numbers
0       12  8   0         0            1            x        x
1       12  8   0         0            1            0        20
  # verify that output persists through falling edge
0       0   0   0         0            1            0        20

# add two numbers with carry
0       8   8   0         0            1            x        x
1       8   8   1         0            1            0        17
  # verify that output persists through falling edge
  # carry flag is latched in the flags, so it's unexpected for it to change on the falling edge
  # if it did, the result would change
0       0   0   1         0            1            0        17

# add two numbers that overflow
0       255 1   0         0            1            x        x
1       255 1   0         0            1            1        0

# add 255 + carry = overflow
0       255 0   1         0            1            x        x
1       255 0   1         0            1            1        0

# add two numbers that overflow and nonzero result
0       128 255 0         0            1            x        x
1       128 255 0         0            1            1        127
*/
