// Digital circuit alu.dig as structural Verilog
module alu (
  input  SelectA,
  input  SelectB,
  input  [7:0] LHSIn,
  input  CarryIn,
  input  [7:0] RHSIn,
  input  ClockIn,
  output CarryOut,
  output [7:0] AdderOut
);

  wire adder_1_carryout, ZeroFlag;
  wire [7:0] CarryFlag;

  // shift shift_1: pin names not known; wires that end beside it: CarryIn, RHSIn, CarryFlag
  adder adder_1 (
    .ClockIn(ClockIn), .LHS(CarryFlag), .CarryOut(adder_1_carryout), .AdderOut(AdderOut));  // open: RHS, CarryIn
  // flags flags_1: pin names not known; wires that end beside it: ClockIn, adder_1_carryout, AdderOut, CarryOut, CarryFlag, ZeroFlag
endmodule
