// Digital circuit flags.dig as structural Verilog
module flags (
  input  ClockIn,
  input  ArithCarryIn,
  input  [7:0] DataIn,
  input  LogicCarryIn,
  output ArithCarryFlag,
  output ZeroFlag,
  output LogicCarryFlag
);

  wire _74260_1_pin5, _74260_1_pin6, NC;

  and and_1 (ZeroFlag, _74260_1_pin6, _74260_1_pin5);
  _74260 _74260_1 (
    .pin1(DataIn[0]), .pin2(DataIn[1]), .pin3(DataIn[2]), .pin4(DataIn[4]), .pin5(_74260_1_pin5),
    .pin6(_74260_1_pin6), .pin7(1'b0), .pin8(1'b0), .pin9(DataIn[7]), .pin10(DataIn[6]), .pin11(DataIn[5]),
    .pin12(DataIn[3]), .pin13(1'b0), .pin14(1'b1));
  _74574 _74574_1 (
    .pin1(1'b0), .pin2(1'b0), .pin3(1'b0), .pin4(1'b0), .pin5(1'b0), .pin6(1'b0), .pin7(1'b0),
    .pin8(LogicCarryIn), .pin9(ArithCarryIn), .pin10(1'b0), .pin11(ClockIn), .pin12(ArithCarryFlag),
    .pin13(LogicCarryFlag), .pin14(NC), .pin15(NC), .pin16(NC), .pin17(NC), .pin18(NC), .pin19(NC),
    .pin20(1'b1));
endmodule

/* Test case Zero Flag Tests:
ClockIn DataIn ZeroFlag
0       12     x
C       12     0
C       0      1
C       1      0
*/

/* Test case Arith Carry Flag Tests:
ClockIn ArithCarryIn ArithCarryFlag
0       0            x
C       1            1
C       0            0
*/

/* Test case Logic Carry Flag Tests:
ClockIn LogicCarryIn LogicCarryFlag
0       0            x
C       1            1
C       0            0
*/
