// Digital circuit shift.dig as structural Verilog
module shift (
  input  SelectA,
  input  SelectB,
  input  [7:0] LHSIn,
  input  CarryIn,
  output CarryOut,
  output [7:0] LHSOut
);

  _74253 _74253_1 (
    .pin1(1'b0), .pin2(SelectB), .pin3(1'b0), .pin4(LHSIn[1]), .pin5(CarryIn), .pin6(LHSIn[0]),
    .pin7(LHSOut[0]), .pin8(1'b0), .pin9(LHSOut[1]), .pin10(LHSIn[1]), .pin11(LHSIn[0]), .pin12(LHSIn[2]),
    .pin13(1'b0), .pin14(SelectA), .pin15(1'b0), .pin16(1'b1));
  _74253 _74253_2 (
    .pin1(1'b0), .pin2(SelectB), .pin3(1'b0), .pin4(LHSIn[3]), .pin5(LHSIn[1]), .pin6(LHSIn[2]),
    .pin7(LHSOut[2]), .pin8(1'b0), .pin9(LHSOut[3]), .pin10(LHSIn[3]), .pin11(LHSIn[2]), .pin12(LHSIn[4]),
    .pin13(1'b0), .pin14(SelectA), .pin15(1'b0), .pin16(1'b1));
  _74253 _74253_3 (
    .pin1(1'b0), .pin2(SelectB), .pin3(1'b0), .pin4(LHSIn[5]), .pin5(LHSIn[3]), .pin6(LHSIn[4]),
    .pin7(LHSOut[4]), .pin8(1'b0), .pin9(LHSOut[5]), .pin10(LHSIn[5]), .pin11(LHSIn[4]), .pin12(LHSIn[6]),
    .pin13(1'b0), .pin14(SelectA), .pin15(1'b0), .pin16(1'b1));
  _74253 _74253_4 (
    .pin1(1'b0), .pin2(SelectB), .pin3(1'b0), .pin4(LHSIn[7]), .pin5(LHSIn[5]), .pin6(LHSIn[6]),
    .pin7(LHSOut[6]), .pin8(1'b0), .pin9(LHSOut[7]), .pin10(LHSIn[7]), .pin11(LHSIn[6]), .pin12(CarryIn),
    .pin13(1'b0), .pin14(SelectA), .pin15(1'b0), .pin16(1'b1));
  _74253 _74253_5 (
    .pin1(1'b0), .pin2(SelectB), .pin3(1'b0), .pin4(LHSIn[0]), .pin5(LHSIn[7]), .pin6(CarryIn),
    .pin7(CarryOut), .pin8(1'b0), .pin10(1'b0), .pin11(1'b0), .pin12(1'b0), .pin13(1'b0), .pin14(SelectA),
    .pin15(1'b0), .pin16(1'b1));  // open: pin9
endmodule

/* Test case Basic Tests:
SelectB SelectA CarryIn    LHSIn      LHSOut     CarryOut
# unchanged
0       0       0          0          0          0
0       0       0          0xff       0xff       0
0       0       1          0          0          1

# left shift
0       1       0          0b00000000 0b00000000 0
0       1       0          0b11111111 0b11111110 1
0       1       1          0b11111111 0b11111111 1

# right shift
1       0       0          0b00000000 0b00000000 0
1       0       0          0b11111111 0b01111111 1
1       0       1          0b11111111 0b11111111 1

# zero
1       1       0          0xff       0x00       0
1       1       1          0xff       0x00       0
*/
