// Digital circuit mainbus.dig as structural Verilog
module mainbus (
  input  ClockIn,
  input  LHS__0,
  input  LHS__1,
  input  RHS__0,
  input  RHS__1,
  input  MainBus__Assert__0,
  input  MainBus__Assert__1,
  input  MainBus__Assert__2,
  input  MainBus__Assert__3,
  input  MainBus__Load__0,
  input  MainBus__Load__1,
  input  MainBus__Load__2,
  input  MainBus__Load__3,
  input  [7:0] MainBus,
  input  Inc__PCRA__0,
  input  Inc__PCRA__1,
  input  Inc__SPSIDI__0,
  input  Inc__SPSIDI__1,
  input  Xfer__Assert0,
  input  Xfer__Assert1,
  input  Xfer__Assert2,
  input  Xfer__LoadDec0,
  input  Xfer__LoadDec1,
  input  Xfer__LoadDec2,
  input  Xfer__LoadDec3,
  input  AddrSel0,
  input  AddrSel1,
  input  AddrSel2,
  input  Reset,
  input  [7:0] LHSBus,
  input  [7:0] RHSBus
);

  wire dipswitch_1_out, dipswitch_2_out, dipswitch_3_out, Reg__A__Assert, Reg__A__LHS, Reg__A__Load,
       Reg__A__RHS, Reg__B__Assert, Reg__B__LHS, Reg__B__Load, Reg__B__RHS, Reg__C__Assert, Reg__C__LHS,
       Reg__C__Load, Reg__C__RHS, Reg__D__Assert, Reg__D__LHS, Reg__D__Load, Reg__D__RHS;
  wire [7:0] LHSBus_t, MainBus_t, RHSBus_t;

  // buscontrol buscontrol_1: pin names not known; wires that end beside it: ClockIn, LHS__0, LHS__1, RHS__0, RHS__1, Reset, MainBus__Assert__0, MainBus__Assert__1, MainBus__Assert__2, MainBus__Assert__3, MainBus__Load__0, MainBus__Load__1, MainBus__Load__2, MainBus__Load__3, Inc__PCRA__0, Inc__PCRA__1, Inc__SPSIDI__0, Inc__SPSIDI__1, Xfer__Assert0, Xfer__Assert1, Xfer__Assert2, Xfer__LoadDec0, Xfer__LoadDec1, Xfer__LoadDec2, Xfer__LoadDec3, AddrSel0, AddrSel1, AddrSel2, Reg__A__LHS, Reg__B__LHS, Reg__C__LHS, Reg__D__LHS, Reg__A__RHS, Reg__B__RHS, Reg__C__RHS, Reg__D__RHS, Reg__A__Assert, Reg__B__Assert, Reg__C__Assert
  reg_8bit_generalpurpose A (
    .MainBusIn(MainBus_t), .Reg__Assert__RHS(Reg__A__RHS), .Reg__Assert__LHS(Reg__A__LHS),
    .Reg__Assert(Reg__A__Assert), .Reg__Load(Reg__A__Load), .MainBusOut(MainBus_t), .LHSBus(LHSBus_t),
    .RHSBus(RHSBus_t));  // open: RegisterContents
  reg_8bit_generalpurpose B (
    .MainBusIn(MainBus_t), .Reg__Assert__RHS(Reg__B__RHS), .Reg__Assert__LHS(Reg__B__LHS),
    .Reg__Assert(Reg__B__Assert), .Reg__Load(Reg__B__Load), .MainBusOut(MainBus_t), .LHSBus(LHSBus_t),
    .RHSBus(RHSBus_t));  // open: RegisterContents
  reg_8bit_generalpurpose C (
    .MainBusIn(MainBus_t), .Reg__Assert__RHS(Reg__C__RHS), .Reg__Assert__LHS(Reg__C__LHS),
    .Reg__Assert(Reg__C__Assert), .Reg__Load(Reg__C__Load), .MainBusOut(MainBus_t), .LHSBus(LHSBus_t),
    .RHSBus(RHSBus_t));  // open: RegisterContents
  reg_8bit_generalpurpose D (
    .MainBusIn(MainBus_t), .Reg__Assert__RHS(Reg__D__RHS), .Reg__Assert__LHS(Reg__D__LHS),
    .Reg__Assert(Reg__D__Assert), .Reg__Load(Reg__D__Load), .MainBusOut(MainBus_t), .LHSBus(LHSBus_t),
    .RHSBus(RHSBus_t));  // open: RegisterContents
  DipSwitch dipswitch_1 (.out(dipswitch_1_out));
  PullUp #(.Bits(8)) pullup_1 (.out(MainBus_t));
  assign MainBus_t = dipswitch_1_out ? MainBus : 8'bz;  // Driver driver_1
  DipSwitch dipswitch_2 (.out(dipswitch_2_out));
  assign LHSBus_t = dipswitch_2_out ? LHSBus : 8'bz;  // Driver driver_2
  PullUp #(.Bits(8)) pullup_2 (.out(LHSBus_t));
  DipSwitch dipswitch_3 (.out(dipswitch_3_out));
  PullUp #(.Bits(8)) pullup_3 (.out(RHSBus_t));
  assign RHSBus_t = dipswitch_3_out ? RHSBus : 8'bz;  // Driver driver_3

  // Other names for the same wires on the sheet: Clock = ClockIn

  // Notes on the sheet:
  //   MainBus: default 105
  //   LHSBus: default 105
  //   RHSBus: default 105
  //   These Tri-States are temporary, makes it easier to test
endmodule
