// Digital circuit memory.dig as structural Verilog
module memory (
  input  MemBridge__Direction,
  input  MemBridge__Load,
  input  [15:0] AddrIn,
  input  [7:0] MEMDATAIn,
  output [15:0] AddrOut,
  output [7:0] MEMDATAOut
);

  wire not_1_out, not_2_out, not_4_out, nOutputEnable, nRamCE, nRamWE, nRomCE;

  not not_1 (not_1_out, MemBridge__Load);
  not not_2 (not_2_out, not_1_out);
  not not_3 (nOutputEnable, MemBridge__Direction);
  not not_4 (not_4_out, not_2_out);
  _74138 _74138_1 (
    .pin1(AddrIn[15]), .pin2(1'b0), .pin3(1'b0), .pin4(1'b0), .pin5(1'b0), .pin6(1'b1), .pin8(1'b0),
    .pin14(nRamCE), .pin15(nRomCE), .pin16(1'b1));  // open: pin7, pin9, pin10, pin11, pin12, pin13
  not not_5 (nRamWE, not_4_out);
  // _28c256 _28c256_1: pin names not known; wires that end beside it: AddrIn[14], AddrIn[12], AddrIn[7], AddrIn[6], AddrIn[5], AddrIn[4], AddrIn[3], AddrIn[2], AddrIn[1], AddrIn[0], MEMDATAIn[0], MEMDATAIn[1], MEMDATAIn[2], 1'b0, 1'b1, 1'b1, AddrIn[13], AddrIn[8], AddrIn[9], AddrIn[0], nOutputEnable, AddrIn[10], nRomCE, MEMDATAIn[7]
  _62256 _62256_1 (
    .nCE(nRamCE), .nOE(nOutputEnable), .nWE(nRamWE), .VCC(1'b1), .GND(1'b0), .I_O0(MEMDATAIn[0]),
    .I_O1(MEMDATAIn[1]), .I_O2(MEMDATAIn[2]), .I_O3(MEMDATAIn[3]), .I_O4(MEMDATAIn[4]), .I_O5(MEMDATAIn[5]),
    .I_O6(MEMDATAIn[6]), .I_O7(MEMDATAIn[7]), .A0(AddrIn[0]), .A1(AddrIn[1]), .A2(AddrIn[2]), .A3(AddrIn[3]),
    .A4(AddrIn[4]), .A5(AddrIn[5]), .A6(AddrIn[6]), .A7(AddrIn[7]), .A8(AddrIn[8]), .A9(AddrIn[9]),
    .A10(AddrIn[10]), .A11(AddrIn[0]), .A12(AddrIn[12]), .A13(AddrIn[13]), .A14(AddrIn[14]));

  assign AddrOut = AddrIn;
  assign MEMDATAOut = MEMDATAIn;

  // Other names for the same wires on the sheet: Addr[15:0] = AddrIn; Addr0 = AddrIn[0]; Addr1 = AddrIn[1];
  //   Addr2 = AddrIn[2]; Addr3 = AddrIn[3]; Addr4 = AddrIn[4]; Addr5 = AddrIn[5]; Addr6 = AddrIn[6];
  //   Addr7 = AddrIn[7]; Addr8 = AddrIn[8]; Addr9 = AddrIn[9]; Addr10 = AddrIn[10]; Addr11 = AddrIn[11];
  //   Addr12 = AddrIn[12]; Addr13 = AddrIn[13]; Addr14 = AddrIn[14]; Addr15 = AddrIn[15]; MEMDATA[7:0] = MEMDATAIn;
  //   MEMDATA0 = MEMDATAIn[0]; MEMDATA1 = MEMDATAIn[1]; MEMDATA2 = MEMDATAIn[2]; MEMDATA3 = MEMDATAIn[3];
  //   MEMDATA4 = MEMDATAIn[4]; MEMDATA5 = MEMDATAIn[5]; MEMDATA6 = MEMDATAIn[6]; MEMDATA7 = MEMDATAIn[7]
endmodule
