// Digital circuit reg-8bit-generalpurpose.dig as structural Verilog
module reg_8bit_generalpurpose (
  input  [7:0] MainBusIn,
  input  Reg__Assert__RHS,
  input  Reg__Assert__LHS,
  input  Reg__Assert,
  input  Reg__Load,
  output [7:0] MainBusOut,
  output [7:0] LHSBus,
  output [7:0] RHSBus,
  output [7:0] RegisterContents
);

  _74574 _8bit_GPR (
    .pin1(1'b0), .pin2(MainBusIn[7]), .pin3(MainBusIn[6]), .pin4(MainBusIn[5]), .pin5(MainBusIn[4]),
    .pin6(MainBusIn[3]), .pin7(MainBusIn[2]), .pin8(MainBusIn[1]), .pin9(MainBusIn[0]), .pin10(1'b0),
    .pin11(Reg__Load), .pin12(RegisterContents[0]), .pin13(RegisterContents[1]), .pin14(RegisterContents[2]),
    .pin15(RegisterContents[3]), .pin16(RegisterContents[4]), .pin17(RegisterContents[5]),
    .pin18(RegisterContents[6]), .pin19(RegisterContents[7]), .pin20(1'b1));
  _74541 Main_Bus_Driver (
    .pin1(Reg__Assert), .pin2(RegisterContents[7]), .pin3(RegisterContents[6]), .pin4(RegisterContents[5]),
    .pin5(RegisterContents[4]), .pin6(RegisterContents[3]), .pin7(RegisterContents[2]),
    .pin8(RegisterContents[1]), .pin9(RegisterContents[0]), .pin10(1'b0), .pin11(MainBusOut[0]),
    .pin12(MainBusOut[1]), .pin13(MainBusOut[2]), .pin14(MainBusOut[3]), .pin15(MainBusOut[4]),
    .pin16(MainBusOut[5]), .pin17(MainBusOut[6]), .pin18(MainBusOut[7]), .pin19(1'b0), .pin20(1'b1));
  _74541 LHS_Bus_Driver (
    .pin1(Reg__Assert__LHS), .pin2(RegisterContents[7]), .pin3(RegisterContents[6]),
    .pin4(RegisterContents[5]), .pin5(RegisterContents[4]), .pin6(RegisterContents[3]),
    .pin7(RegisterContents[2]), .pin8(RegisterContents[1]), .pin9(RegisterContents[0]), .pin10(1'b0),
    .pin11(LHSBus[0]), .pin12(LHSBus[1]), .pin13(LHSBus[2]), .pin14(LHSBus[3]), .pin15(LHSBus[4]),
    .pin16(LHSBus[5]), .pin17(LHSBus[6]), .pin18(LHSBus[7]), .pin19(1'b0), .pin20(1'b1));
  _74541 RHS_Bus_Driver (
    .pin1(Reg__Assert__RHS), .pin2(RegisterContents[7]), .pin3(RegisterContents[6]),
    .pin4(RegisterContents[5]), .pin5(RegisterContents[4]), .pin6(RegisterContents[3]),
    .pin7(RegisterContents[2]), .pin8(RegisterContents[1]), .pin9(RegisterContents[0]), .pin10(1'b0),
    .pin11(RHSBus[0]), .pin12(RHSBus[1]), .pin13(RHSBus[2]), .pin14(RHSBus[3]), .pin15(RHSBus[4]),
    .pin16(RHSBus[5]), .pin17(RHSBus[6]), .pin18(RHSBus[7]), .pin19(1'b0), .pin20(1'b1));

  // Notes on the sheet:
  //   MainBusIn: default 105
  //   Reg__Assert__RHS: default 1
  //   Reg__Assert__LHS: default 1
  //   Reg__Assert: default 1
  //   Reg__Load: default 1
endmodule
