// Digital circuit pipeline.dig as structural Verilog
module pipeline (
);

  pipeline_stage0 pipeline_stage0_1 ();  // open: MEMDATA, BusRequest, FetchSuppress, Flags__5__PCRA__Flip, ClockIn, Pipe0Out__0__IncPCRA0, Pipe0Out__1__IncPCRA1, Pipe0Out
endmodule
